# Fritzing sketch Schematics (saved by Fritzing 1.0.1rc)

parts:
  A1 = Esp32-c3 super mini
  Sensor1 = TTP223B Capacitive Touch Sensor Module
  Parte1 = InvenSense MPU6050
  U2 = WS2812 RGB LED matrix 4x4
  U1 = LIPO-110mAh [package=lipo-110]
  A4 = DWEII Type-C USB 5V 2A Boost Converter Module

nets:
  N1: A1.Pin_3, U2.DIN
  N2: A1.Pin_4, Parte1.SDA
  N3: A1.Pin_5, Parte1.SCL
  N4: A1.Pin_6, Sensor1.SIG
  N5: A1.Pin_7, Parte1.INT
  VCC: A1.Pin_14, Sensor1.VCC, Parte1.VCC
  GND: A1.Pin_15, Sensor1.GND, Parte1.GND, U2.GND, A4.OUT-
  N6: A1.Pin_16, U2.VCC, A4.OUT+
  N7: U1.+, A4.BAT+
  N8: U1.-, A4.BAT-

custom parts:
  Esp32-c3 super mini: ESP32-C3 Development Board ESP32 SuperMini Development Board ESP32 Development Board WiFi Bluetooth.
  TTP223B Capacitive Touch Sensor Module: The TTP223B capacitive touch sensor module uses the TTP223B IC. The appropriate voltage is approximately 2 to 5.5 volts.
  WS2812 RGB LED matrix 4x4: WS2812 matrix 4x4
